# Fritzing sketch wiring (saved by Fritzing 0.9.3b)
circuit board: 8.46667cm x 5.64444cm

parts:
  Bauteil1 = Arduino Uno (Rev3) - ICSP
  Bauteil2 = Logic Level Converter
  Part1 = KY-019 5V Relay Module [package="Breakout board"]
  Espessif_Serial_Wifi_Modul_1 = ESP8266 ESP01 [part_number=ESP8266 package=THT]
  S1 = SPST Switch [package=switch-spdt_lock.007s]

nets:
  N1: Bauteil1.5V, Bauteil2.HV, Part1.+, S1.P
  N2: Bauteil1.D10_PWM/SS, Bauteil2.TX_HV
  N3: Bauteil1.D11_PWM/MOSI, Bauteil2.RX_HV
  GND: Bauteil1.GND, Bauteil2.GND, Part1.-, Espessif_Serial_Wifi_Modul_1.GND
  N4: Bauteil1.D2, Part1.S
  N5: Bauteil1.D3_PWM, S1.O
  3V3: Bauteil1.3V3, Bauteil2.LV, Espessif_Serial_Wifi_Modul_1.VCC, Espessif_Serial_Wifi_Modul_1.CH_PD
  N6: Bauteil2.RX_LV, Espessif_Serial_Wifi_Modul_1.RXD
  N7: Bauteil2.TX_LV, Espessif_Serial_Wifi_Modul_1.TXD

custom parts:
  KY-019 5V Relay Module: KY-019 5V Relay module, used to control AC circuits.
  ESP8266 ESP01: Generic WiFi Module based on the ESP8266 with onboard PCB antenna and UART communications
